// Logisim project counter8_T.circ as structural Verilog: 1 circuit, main circuit main
module main (
  input  q2,
  input  q1,
  input  q0,
  output T2,
  output T1,
  output T0
);

  and and_1 (T2, q1, q0);

  assign T0 = 1'b1;
  assign T1 = q0;
endmodule
